// Logisim project hkcpu.circ as structural Verilog
module alu (
  input  CLK,
  input  RST,
  input  [15:0] A,
  input  [15:0] B,
  input  [2:0] ALM,
  input  ALO,
  output [2:0] FLG,
  output [15:0] BUSO
);

  wire and_1_out;
  wire [2:0] comparator_1_gt;
  wire [15:0] adder_1_out, divider_1_out, multiplier_1_out, subtractor_1_out;

  Comparator #(.mode("unsigned"), .width(16)) comparator_1 (
    .a(A), .b(B), .gt(comparator_1_gt[0]), .eq(comparator_1_gt[1]), .lt(comparator_1_gt[2]));
  Adder #(.width(16)) adder_1 (.a(A), .b(B), .out(adder_1_out));  // open: cin, cout
  Subtractor #(.width(16)) subtractor_1 (.a(A), .b(B), .out(subtractor_1_out));  // open: bin, bout
  Multiplier #(.width(16)) multiplier_1 (.a(A), .b(B), .out(multiplier_1_out));  // open: cin, cout
  Divider #(.width(16)) divider_1 (.a(A), .b(B), .out(divider_1_out));  // open: upper, rem
  Register #(.width(3)) FLGR (.D(comparator_1_gt), .Q(FLG), .clk(CLK), .clr(RST));  // open: en
  Multiplexer #(.enable("true"), .select(2), .width(16)) multiplexer_1 (
    .in0(adder_1_out), .in1(subtractor_1_out), .in2(multiplier_1_out), .in3(divider_1_out), .out(BUSO),
    .sel(ALM[1:0]), .en(and_1_out));
  and and_1 (and_1_out, ~ALM[2], ALO);  // AND_Gate
endmodule

module regs (
  input  CLK,
  input  RST,
  input  [15:0] BUSI,
  input  [3:0] RGI,
  input  [3:0] RGO,
  output [15:0] BUSO,
  output [15:0] A_BPS,
  output [15:0] B_BPS
);

  wire [15:0] CR_q, DR_q;

  assign BUSO = RGO[0] ? A_BPS : 16'bz;  // Controlled_Buffer controlled_buffer_1
  Register #(.width(16)) AR (.D(BUSI), .en(RGI[0]), .Q(A_BPS), .clk(CLK), .clr(RST));
  assign BUSO = RGO[1] ? B_BPS : 16'bz;  // Controlled_Buffer controlled_buffer_2
  Register #(.width(16)) BR (.D(BUSI), .en(RGI[1]), .Q(B_BPS), .clk(CLK), .clr(RST));
  assign BUSO = RGO[2] ? CR_q : 16'bz;  // Controlled_Buffer controlled_buffer_3
  Register #(.width(16)) CR (.D(BUSI), .en(RGI[2]), .Q(CR_q), .clk(CLK), .clr(RST));
  assign BUSO = RGO[3] ? DR_q : 16'bz;  // Controlled_Buffer controlled_buffer_4
  Register #(.width(16)) DR (.D(BUSI), .en(RGI[3]), .Q(DR_q), .clk(CLK), .clr(RST));
endmodule
